# Fritzing sketch pedi (saved by Fritzing 0.9.0b)
circuit board: 10.5697cm x 6.75971cm
breadboards: 1

parts:
  Longitudes_A-P = screw terminal, 16 pins
  Longitudes_Q-_X = screw terminal, 8 pins
  Latitudes_0-5 = screw terminal, 6 pins
  Mega_Holes = Arduino Mega 2560 (Rev3)
  Latitudes_6_-_Y = screw terminal, 5 pins
  2n3906 = PNP-Transistor [package="TO92 [THT]"]
  Battery = Battery block 9V
  10K = Resistor [tolerance=±5% resistance=220 package=THT]
  R1 = Resistor [tolerance=±5% resistance=220 package=THT]
  10pF = Ceramic Capacitor [capacitance=100nF package="100 mil [THT, multilayer]"]
  LM317 = Voltage Regulator [package=to220-adj]
  12 = Resistor [tolerance=±5% resistance=220 package=THT]

nets:
  N1: Longitudes_A-P.pin1, Mega_Holes.D22
  N2: Longitudes_A-P.pin2, Mega_Holes.D24
  N3: Longitudes_A-P.pin3, Mega_Holes.D26
  N4: Longitudes_A-P.pin4, Mega_Holes.D28
  N5: Longitudes_A-P.pin5, Mega_Holes.D30
  N6: Longitudes_A-P.pin6, Mega_Holes.D32
  N7: Longitudes_A-P.pin7, Mega_Holes.D34
  N8: Longitudes_A-P.pin8, Mega_Holes.D36
  N9: Longitudes_A-P.pin9, Mega_Holes.D38
  N10: Longitudes_A-P.pin10, Mega_Holes.D40
  N11: Longitudes_A-P.pin11, Mega_Holes.D42
  N12: Longitudes_A-P.pin12, Mega_Holes.D44
  N13: Longitudes_A-P.pin13, Mega_Holes.D46
  N14: Longitudes_A-P.pin14, Mega_Holes.D48
  N15: Longitudes_A-P.pin15, Mega_Holes.D50
  N16: Longitudes_A-P.pin16, Mega_Holes.D52
  N17: Longitudes_Q-_X.pin1, Mega_Holes.D23
  N18: Longitudes_Q-_X.pin2, Mega_Holes.D25
  N19: Longitudes_Q-_X.pin3, Mega_Holes.D27
  N20: Longitudes_Q-_X.pin4, Mega_Holes.D29
  N21: Longitudes_Q-_X.pin5, Mega_Holes.D31
  N22: Longitudes_Q-_X.pin6, Mega_Holes.D33
  N23: Longitudes_Q-_X.pin7, Mega_Holes.D35
  N24: Longitudes_Q-_X.pin8, Mega_Holes.D37
  N25: Latitudes_0-5.pin1, Mega_Holes.D7_PWM
  N26: Latitudes_0-5.pin2, Mega_Holes.D6_PWM
  N27: Latitudes_0-5.pin3, Mega_Holes.D5_PWM
  N28: Latitudes_0-5.pin4, Mega_Holes.D4_PWM
  N29: Latitudes_0-5.pin5, Mega_Holes.D3_PWM
  N30: Latitudes_0-5.pin6, Mega_Holes.D2_PWM
  N31: Mega_Holes.D11_PWM, Latitudes_6_-_Y.pin2, 2n3906.B
  N32: Mega_Holes.D10_PWM, Latitudes_6_-_Y.pin3
  N33: Mega_Holes.D9_PWM, Latitudes_6_-_Y.pin4
  N34: Mega_Holes.D8_PWM, Latitudes_6_-_Y.pin5
  N35: Latitudes_6_-_Y.pin1, R1.Pin_1
  N36: 2n3906.E, Battery.-, 10pF.1
  N37: 2n3906.C, 10K.Pin_1, 10pF.0
  N38: Battery.+, 10K.Pin_0, R1.Pin_0, LM317.IN
  N39: LM317.ADJ, 12.Pin_0
  N40: LM317.OUT, 12.Pin_1

notes:
  A
  B
  C
  D
  E
  F
  G
  H
  I
  J
  K
  L
  M
  N
  O
  P
  Mega Mont for Pediatric Perimeter
  Q
  R
  S
  T
  U
  V
  W
  X
  0
  1
  2
  3
  4
  6
  7
  8
  9
  Y
  5
  Srujana Innovation at
  LVPEI
  Rev 0.1.2
  So that all may see
